# Fritzing sketch schematic (saved by Fritzing 1.0.5)
circuit board: 8.46667cm x 5.64444cm

parts:
  esp32 = ESP32 DevKitc V4
  A1 = nrf24l01+palna
  M1 = cc1101 module  # not connected

nets:
  N1: esp32.IO15, A1.Pin_6
  N2: esp32.IO16, A1.Pin_2
  N3: esp32.3V3, A1.Pin_5
  N4: esp32.IO14, A1.Pin_3
  N5: esp32.IO12, A1.Pin_4
  N6: esp32.GND#32, A1.Pin_1
  N7: esp32.IO13, A1.Pin_7

custom parts:
  ESP32 DevKitc V4: ESP32-DevKitC board with ESP32-WROOM-32 module. ESP32-DevKitC V4 is a small-sized ESP32-based development board produced by Espressif. Most of the pins on the ESP module are broken out to the pin headers on the board. The pins D0, D1, D2, D3, CMD and CLK are used internally for communication between ESP32 and SPI flash memory. They are grouped on both sides near the USB connector. Avoid using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
  cc1101 module: CC1101 rf module.
